// Logisim project Lab_4.circ as structural Verilog: 6 circuits, main circuit Асинхронный RS триггер с прямыми входами
module \Асинхронный_RS_триггер_с_прямыми_входами  (
  input  in_1,
  input  in_2,
  output out_3,
  output out_4
);

  nor nor_1 (out_3, in_1, out_4);
  nor nor_2 (out_4, out_3, in_2);
endmodule

module \Асинхронный_RS_триггер_с_инверсными_входами  (
  input  in_1,
  input  in_2,
  output out_3,
  output out_4
);

  nand nand_1 (out_3, in_1, out_4);
  nand nand_2 (out_4, out_3, in_2);
endmodule

module \Синхронный_RS_триггер  (
  input  in_1,
  input  in_2,
  input  in_3,
  output out_4,
  output out_5
);

  wire nand_1_out, nand_2_out;

  nand nand_1 (nand_1_out, in_1, in_1, in_2);
  nand nand_2 (nand_2_out, in_2, in_3);
  nand nand_3 (out_4, nand_1_out, out_5);
  nand nand_4 (out_5, out_4, nand_2_out);
endmodule

module \S_триггер  (
  input  in_1,
  input  in_2,
  output out_3,
  output out_4
);

  wire nand_1_out, nand_2_out;

  nand nand_1 (nand_1_out, in_1, in_1);
  nand nand_2 (nand_2_out, nand_1_out, in_2);
  nand nand_3 (out_3, nand_1_out, out_4);
  nand nand_4 (out_4, out_3, nand_2_out);
endmodule

module \R_триггер  (
  input  in_1,
  input  in_2,
  output out_3,
  output out_4
);

  wire nand_1_out, nand_2_out;

  nand nand_1 (nand_1_out, in_1, nand_2_out);
  nand nand_2 (nand_2_out, in_2, in_2);
  nand nand_3 (out_3, nand_1_out, out_4);
  nand nand_4 (out_4, out_3, nand_2_out);
endmodule

module \E_триггер  (
  input  in_1,
  input  in_2,
  output out_3,
  output out_4
);

  wire nand_1_out, nand_2_out, nand_3_out, nand_4_out;

  nand nand_1 (nand_1_out, in_1, in_1);
  nand nand_2 (nand_2_out, in_2, in_2);
  nand nand_3 (nand_3_out, in_1, nand_2_out);
  nand nand_4 (nand_4_out, nand_1_out, in_2);
  nand nand_5 (out_3, nand_3_out, nand_3_out, out_4);
  nand nand_6 (out_4, out_3, nand_4_out);
endmodule
