// Logisim project Lab_5.circ as structural Verilog: 3 circuits, main circuit D триггер
module \D_триггер  (
  input  D,
  input  \С ,
  output out_3,
  output out_4
);

  wire nand_1_out, nand_2_out;

  nand nand_1 (nand_1_out, D, \С );
  nand nand_2 (nand_2_out, nand_1_out, \С );
  nand nand_3 (out_3, nand_1_out, out_4);
  nand nand_4 (out_4, out_3, nand_2_out);
endmodule

module \T_триггре  (
  input  in_1,
  input  in_2,
  input  in_3,
  output out_4,
  output out_5
);

  wire nand_1_out, nand_2_out, nand_3_out;

  nand nand_1 (nand_1_out, in_2, in_3);
  nand nand_2 (nand_2_out, in_1, nand_1_out);
  nand nand_3 (nand_3_out, nand_2_out, nand_1_out);
  nand nand_4 (out_4, nand_2_out, out_5);
  nand nand_5 (out_5, out_4, nand_3_out);
endmodule

module \JK_триггер  (
  input  K,
  input  C,
  input  J,
  output out_4,
  output out_5
);

  wire and_1_out, and_2_out, nand_1_out, nand_2_out, nand_3_out, nand_4_out, nand_5_out, nand_6_out,
       not_1_out;

  and and_1 (and_1_out, out_4, K);
  and and_2 (and_2_out, J, out_5);
  nand nand_1 (nand_1_out, and_1_out, C);
  nand nand_2 (nand_2_out, C, and_2_out);
  not not_1 (not_1_out, C);
  nand nand_3 (nand_3_out, nand_1_out, nand_4_out);
  nand nand_4 (nand_4_out, nand_3_out, nand_2_out);
  nand nand_5 (nand_5_out, nand_3_out, not_1_out);
  nand nand_6 (nand_6_out, not_1_out, nand_4_out);
  nand nand_7 (out_4, nand_5_out, out_5);
  nand nand_8 (out_5, out_4, nand_6_out);
endmodule
