// Logisim project Lab_6.circ as structural Verilog: 4 circuits, main circuit main
module main (
  input  in_1,
  input  in_2,
  output out_3
);

  wire and_1_out, and_2_out, not_1_out, not_2_out;

  not not_1 (not_1_out, in_1);
  not not_2 (not_2_out, in_2);
  and and_1 (and_1_out, not_1_out, in_2);
  and and_2 (and_2_out, in_1, not_2_out);
  or or_1 (out_3, and_1_out, and_2_out);
endmodule

module \Полусумматор  (
  input  in_1,
  input  in_2,
  output out_3,
  output out_4
);

  wire and_2_out, and_3_out, not_1_out, not_2_out;

  and and_1 (out_3, in_1, in_2);
  not not_1 (not_1_out, in_1);
  not not_2 (not_2_out, in_2);
  and and_2 (and_2_out, not_1_out, in_2);
  and and_3 (and_3_out, in_1, not_2_out);
  or or_1 (out_4, and_2_out, and_3_out);
endmodule

module \Сумматор  (
  input  in_1,
  input  in_2,
  input  in_3,
  output out_4,
  output out_5
);

  wire and_1_out, and_2_out, and_3_out, and_4_out, and_5_out, and_6_out, not_1_out, not_2_out, not_3_out,
       not_4_out, or_1_out;

  and and_1 (and_1_out, in_1, in_2);
  not not_1 (not_1_out, in_1);
  not not_2 (not_2_out, in_2);
  and and_2 (and_2_out, not_1_out, in_2);
  and and_3 (and_3_out, in_1, not_2_out);
  or or_1 (or_1_out, and_2_out, and_3_out);
  and and_4 (and_4_out, or_1_out, in_3);
  or or_2 (out_4, and_1_out, and_4_out);
  not not_3 (not_3_out, or_1_out);
  not not_4 (not_4_out, in_3);
  and and_5 (and_5_out, not_3_out, in_3);
  and and_6 (and_6_out, or_1_out, not_4_out);
  or or_3 (out_5, and_5_out, and_6_out);
endmodule

module \Доп_задание  (
  input  in_1,
  input  in_2,
  input  in_3,
  input  in_4,
  input  in_5,
  input  in_6,
  input  in_7,
  input  in_8,
  input  in_9,
  output out_10,
  output out_11,
  output out_12,
  output out_13,
  output out_14
);

  wire and_1_out, and_2_out, and_3_out, and_4_out, and_5_out, and_6_out, and_7_out, and_8_out, and_9_out,
       and_10_out, and_11_out, and_12_out, and_13_out, and_14_out, and_15_out, and_16_out, and_17_out,
       and_18_out, and_19_out, and_20_out, and_21_out, and_22_out, and_23_out, and_24_out, not_1_out,
       not_2_out, not_3_out, not_4_out, not_5_out, not_6_out, not_7_out, not_8_out, not_9_out, not_10_out,
       not_11_out, not_12_out, not_13_out, not_14_out, not_15_out, not_16_out, or_1_out, or_2_out, or_4_out,
       or_5_out, or_7_out, or_8_out, or_10_out;

  and and_1 (and_1_out, in_7, in_8);
  not not_1 (not_1_out, in_7);
  not not_2 (not_2_out, in_8);
  and and_2 (and_2_out, not_1_out, in_8);
  and and_3 (and_3_out, in_7, not_2_out);
  or or_1 (or_1_out, and_2_out, and_3_out);
  and and_4 (and_4_out, or_1_out, in_9);
  or or_2 (or_2_out, and_1_out, and_4_out);
  not not_3 (not_3_out, or_1_out);
  not not_4 (not_4_out, in_9);
  and and_5 (and_5_out, not_3_out, in_9);
  and and_6 (and_6_out, or_1_out, not_4_out);
  and and_7 (and_7_out, in_5, in_6);
  or or_3 (out_14, and_5_out, and_6_out);
  not not_5 (not_5_out, in_5);
  not not_6 (not_6_out, in_6);
  and and_8 (and_8_out, not_5_out, in_6);
  and and_9 (and_9_out, in_5, not_6_out);
  or or_4 (or_4_out, and_8_out, and_9_out);
  and and_10 (and_10_out, or_4_out, or_2_out);
  or or_5 (or_5_out, and_7_out, and_10_out);
  not not_7 (not_7_out, or_4_out);
  not not_8 (not_8_out, or_2_out);
  and and_11 (and_11_out, in_3, in_4);
  not not_9 (not_9_out, in_3);
  not not_10 (not_10_out, in_4);
  and and_12 (and_12_out, not_7_out, or_2_out);
  and and_13 (and_13_out, or_4_out, not_8_out);
  or or_6 (out_13, and_12_out, and_13_out);
  and and_14 (and_14_out, not_9_out, in_4);
  and and_15 (and_15_out, in_3, not_10_out);
  or or_7 (or_7_out, and_14_out, and_15_out);
  and and_16 (and_16_out, or_7_out, or_5_out);
  not not_11 (not_11_out, or_7_out);
  not not_12 (not_12_out, or_5_out);
  and and_17 (and_17_out, in_1, in_2);
  or or_8 (or_8_out, and_11_out, and_16_out);
  not not_13 (not_13_out, in_1);
  not not_14 (not_14_out, in_2);
  and and_18 (and_18_out, not_11_out, or_5_out);
  and and_19 (and_19_out, or_7_out, not_12_out);
  and and_20 (and_20_out, not_13_out, in_2);
  and and_21 (and_21_out, in_1, not_14_out);
  or or_9 (out_12, and_18_out, and_19_out);
  or or_10 (or_10_out, and_20_out, and_21_out);
  and and_22 (and_22_out, or_10_out, or_8_out);
  or or_11 (out_10, and_17_out, and_22_out);
  not not_15 (not_15_out, or_10_out);
  not not_16 (not_16_out, or_8_out);
  and and_23 (and_23_out, not_15_out, or_8_out);
  and and_24 (and_24_out, or_10_out, not_16_out);
  or or_12 (out_11, and_23_out, and_24_out);
endmodule
