// Logisim project Lab_7.circ as structural Verilog: 5 circuits, main circuit main
module main (
  input  in_1,
  input  in_2,
  input  in_3,
  output out_4
);

  wire and_1_out, and_2_out, not_1_out;

  not not_1 (not_1_out, in_3);
  and and_1 (and_1_out, in_1, not_1_out);
  and and_2 (and_2_out, in_2, in_3);
  or or_1 (out_4, and_1_out, and_2_out);
endmodule

module \_4х_канальный_мультиплексор  (
  input  in_1,
  input  in_2,
  input  in_3,
  input  in_4,
  input  in_5,
  input  in_6,
  output out_7
);

  wire and_1_out, and_2_out, and_3_out, and_4_out, not_1_out, not_2_out;

  not not_1 (not_1_out, in_1);
  not not_2 (not_2_out, in_2);
  and and_1 (and_1_out, not_1_out, not_2_out, in_3);
  and and_2 (and_2_out, not_2_out, in_1, in_4);
  and and_3 (and_3_out, not_1_out, in_5, in_2);
  and and_4 (and_4_out, in_1, in_6, in_2);
  or or_1 (out_7, and_1_out, and_2_out, and_3_out, and_4_out);
endmodule

module \_16ти_канальный_мультиплексор  (
  input  D0,
  input  D1,
  input  D2,
  input  D3,
  input  D4,
  input  D5,
  input  D6,
  input  D7,
  input  D8,
  input  D9,
  input  in_11,
  input  in_12,
  input  in_13,
  input  in_14,
  input  in_15,
  input  in_16,
  input  in_17,
  input  in_18,
  input  A2,
  input  A3,
  output out_21
);

  wire and_1_out, and_2_out, and_3_out, and_4_out, and_5_out, and_6_out, and_7_out, and_8_out, and_9_out,
       and_10_out, and_11_out, and_12_out, and_13_out, and_14_out, and_15_out, and_16_out, and_17_out,
       and_18_out, and_19_out, and_20_out, not_1_out, not_2_out, not_3_out, not_4_out, not_5_out, not_6_out,
       not_7_out, not_8_out, not_9_out, not_10_out, or_1_out, or_2_out, or_3_out, or_4_out;

  not not_1 (not_1_out, in_17);
  not not_2 (not_2_out, in_18);
  not not_3 (not_3_out, in_17);
  not not_4 (not_4_out, in_18);
  not not_5 (not_5_out, in_17);
  not not_6 (not_6_out, in_18);
  not not_7 (not_7_out, in_17);
  not not_8 (not_8_out, in_18);
  and and_1 (and_1_out, not_1_out, not_2_out, D0);
  and and_2 (and_2_out, not_2_out, in_17, D1);
  and and_3 (and_3_out, not_1_out, D2, in_18);
  and and_4 (and_4_out, in_17, D3, in_18);
  and and_5 (and_5_out, not_3_out, not_4_out, D4);
  and and_6 (and_6_out, not_4_out, in_17, D5);
  and and_7 (and_7_out, not_3_out, D6, in_18);
  and and_8 (and_8_out, in_17, D7, in_18);
  and and_9 (and_9_out, not_5_out, not_6_out, D8);
  and and_10 (and_10_out, not_6_out, in_17, D9);
  and and_11 (and_11_out, not_5_out, in_11, in_18);
  and and_12 (and_12_out, in_17, in_12, in_18);
  and and_13 (and_13_out, not_7_out, not_8_out, in_13);
  and and_14 (and_14_out, not_8_out, in_17, in_14);
  and and_15 (and_15_out, not_7_out, in_15, in_18);
  and and_16 (and_16_out, in_17, in_16, in_18);
  or or_1 (or_1_out, and_1_out, and_2_out, and_3_out, and_4_out);
  or or_2 (or_2_out, and_5_out, and_6_out, and_7_out, and_8_out);
  or or_3 (or_3_out, and_9_out, and_10_out, and_11_out, and_12_out);
  or or_4 (or_4_out, and_13_out, and_14_out, and_15_out, and_16_out);
  not not_9 (not_9_out, A2);
  not not_10 (not_10_out, A3);
  and and_17 (and_17_out, not_9_out, not_10_out, or_1_out);
  and and_18 (and_18_out, not_10_out, A2, or_2_out);
  and and_19 (and_19_out, not_9_out, or_3_out, A3);
  and and_20 (and_20_out, A2, or_4_out, A3);
  or or_5 (out_21, and_17_out, and_18_out, and_19_out, and_20_out);

  // Notes on the sheet:
  //   D10
  //   D11
  //   D12
  //   D13
  //   D14
  //   D15
  //   A0
  //   A1
endmodule

module \Демультиплексор  (
  input  in_1,
  input  in_2,
  output out_3,
  output out_4
);

  wire not_1_out;

  not not_1 (not_1_out, in_2);
  and and_1 (out_3, in_1, not_1_out);
  and and_2 (out_4, in_1, in_2);
endmodule

module \_16ти_канальный_мультиплексор_из_стандартных_элементов  (
  input  in_1,
  input  in_2,
  input  in_3,
  input  in_4,
  input  in_5,
  input  in_6,
  input  in_7,
  input  in_8,
  input  in_9,
  input  in_10,
  input  in_11,
  input  in_12,
  input  in_13,
  input  in_14,
  input  in_15,
  input  in_16,
  input  [1:0] in_17,
  input  [1:0] in_18,
  output out_19
);

  wire multiplexer_1_out, multiplexer_2_out, multiplexer_3_out, multiplexer_4_out;

  Multiplexer #(.select(2)) multiplexer_1 (
    .in0(in_1), .in1(in_2), .in2(in_3), .in3(in_4), .out(multiplexer_1_out), .sel(in_17));  // open: en
  Multiplexer #(.select(2)) multiplexer_2 (
    .in0(in_5), .in1(in_6), .in2(in_7), .in3(in_8), .out(multiplexer_2_out), .sel(in_17));  // open: en
  Multiplexer #(.select(2)) multiplexer_3 (
    .in0(in_9), .in1(in_10), .in2(in_11), .in3(in_12), .out(multiplexer_3_out), .sel(in_17));  // open: en
  Multiplexer #(.select(2)) multiplexer_4 (
    .in0(in_13), .in1(in_14), .in2(in_15), .in3(in_16), .out(multiplexer_4_out), .sel(in_17));  // open: en
  Multiplexer #(.select(2)) multiplexer_5 (
    .in0(multiplexer_1_out), .in1(multiplexer_2_out), .in2(multiplexer_3_out), .in3(multiplexer_4_out),
    .out(out_19), .sel(in_18));  // open: en
endmodule
