// Logisim project Lab_8.circ as structural Verilog: 1 circuit, main circuit main
module main (
);

  wire and_1_out, and_2_out, button_1_out, not_1_out;
  wire [3:0] counter_1_q, multiplexer_1_out, ram_1_data, register_2_q, register_3_q;
  wire [7:0] adder_1_out, multiplexer_2_out, register_1_q, register_4_q;
  wire [7:4] ram_1_data_2;

  Counter #(.width(4), .max('h4)) counter_1 (.Q(counter_1_q), .clk(button_1_out));  // open: load, D, count, carry, clr
  Button button_1 (.out(button_1_out));
  Multiplexer #(.width(4)) multiplexer_1 (
    .in0(counter_1_q), .in1(register_2_q), .out(multiplexer_1_out), .sel(not_1_out));  // open: en
  not not_1 (not_1_out, button_1_out);
  RAM #(.addrWidth(4), .bus("separate")) ram_1 (
    .addr(multiplexer_1_out), .din(register_4_q), .data({ram_1_data_2, ram_1_data}), .clk(and_1_out));  // open: str, sel, ld, clr
  and and_1 (and_1_out, button_1_out, register_3_q[1]);
  // Probe on register_1_q
  Register register_1 (.D({ram_1_data_2, ram_1_data}), .Q(register_1_q), .clk(and_2_out));  // open: en, clr
  Register #(.width(4)) register_2 (.D(ram_1_data), .Q(register_2_q), .clk(not_1_out));  // open: en, clr
  // Probe on adder_1_out
  Adder adder_1 (.a(register_4_q), .b(register_1_q), .out(adder_1_out));  // open: cin, cout
  Register #(.width(4)) register_3 (.D(ram_1_data_2), .Q(register_3_q), .clk(not_1_out));  // open: en, clr
  Multiplexer #(.width(8)) multiplexer_2 (
    .in0(adder_1_out), .in1(register_1_q), .out(multiplexer_2_out), .sel(register_3_q[2]));  // open: en
  and and_2 (and_2_out, register_3_q[0], not_1_out);
  Register register_4 (.D(multiplexer_2_out), .Q(register_4_q), .clk(button_1_out));  // open: en, clr

  // Notes on the sheet:
  //   Архитектура фон Неймана
endmodule
